# Fritzing sketch DSH (saved by Fritzing 0.9.3b)

parts:
  Componente1 = Arduino Mega 2560 (Rev3)
  Componente3 = RFID-RC522-v3
  Componente4 = FONA 808 Shield

nets:
  N1: Componente1.D19/RX1, Componente4.RX
  N2: Componente1.D18/TX1, Componente4.TX
  GND: Componente1.GND, Componente4.GND
  N3: Componente1.D50, Componente3.IRQ
  N4: Componente1.D51, Componente3.MISO
  N5: Componente1.D52, Componente3.MOSI
  N6: Componente1.D53, Componente3.SCK

custom parts:
  RFID-RC522-v3: A simple China made RFID-RC522 Reader (6x4 cm); do check the pin labels, as this is a MFRC522 based clone.
  FONA 808 Shield: Cellular + GPS tracking, all in one, for your Arduino? Oh yes! Introducing Adafruit FONA 808 GSM + GPS Shield, an all-in-one cellular phone module with that lets you add location-tracking, voice, text, SMS and data to your project, in Arduino shield format for easy use.
